# Fritzing sketch Board (saved by Fritzing 0.9.3b)
circuit board: 3.25978cm x 8.12936cm
breadboards: 1

parts:
  JP1 = Header 1 [package=1x01_offset]  # not connected
  JP2 = Header 1 [package=1x01_offset]
  JP3 = Header 1 [package=1x01_offset]
  JP6 = Header 1 [package=1x01_offset]
  JP4 = Header 1 [package=1x01_offset]
  JP5 = Header 1 [package=1x01_offset]
  JP7 = Header 1 [package=1x01_offset]
  JP9 = Header 1 [package=1x01_offset]
  JP8 = Header 1 [package=1x01_offset]
  JP10 = Header 1 [package=1x01_offset]
  JP12 = Header 1 [package=1x01_offset]
  JP11 = Header 1 [package=1x01_offset]
  JP15 = Header 1 [package=1x01_offset]
  JP13 = Header 1 [package=1x01_offset]  # not connected
  JP14 = Header 1 [package=1x01_offset]
  Componente2 = Arduino Nano (Rev3.0)
  Componente3 = Bluetooth HC-05 Macho

nets:
  N1: JP2.1, Componente2.D11/MOSI
  5V: JP3.1, JP6.1, JP9.1, JP12.1, JP15.1, Componente2.5V, Componente3.VCC
  N2: JP4.1, JP10.1
  N3: JP5.1, Componente2.D9
  GND: JP7.1, Componente2.GND, Componente3.GND
  N4: JP8.1, Componente2.D5
  N5: JP11.1, Componente2.D6
  N6: JP14.1, Componente2.D10
  N7: Componente2.D1/TX, Componente3.RXD
  N8: Componente2.D0/RX, Componente3.TXD
